// Logisim project logic9.circ as structural Verilog: 32 circuits, main circuit main
module main (
  input  in_1,
  output [3:0] SR1_OP2,
  output CF,
  output [3:0] SR2,
  output [17:0] REG1_VALUE,
  output [17:0] ALU_OUTPUT,
  output [17:0] REG2_VALUE,
  output out_8,
  output out_9,
  output [19:0] out_10,
  output [1:0] out_11
);

  wire and_1_out, and_2_out, and_3_out, and_4_out, and_5_out, CLOCK, controlled_buffer_1_out,
       controlled_buffer_2_out, ENABLE_JUMP, ENABLE_PC, IS_ALU, IS_CMP, IS_IMM, IS_JA, IS_JAE, IS_JB, IS_JBE,
       IS_JE, IS_JUMP, IS_LD, IS_ST, JUMP, NEXT_INSTRUCTION, not_1_out, not_2_out, not_3_out, not_4_out,
       not_5_out, not_6_out, not_7_out, WRITE_ENABLE;
  wire [0:0] or_1_out;
  wire [1:0] controlled_buffer_4_out, multiplexer_2_out;
  wire [2:0] n18_bit_comparer_1_a_b;
  wire [3:0] DR_SR_OP2;
  wire [5:0] IMM_6;
  wire [9:0] ADDER_sum, ADDRESS1, ADDRESS2, LAST_ADDRESS, program_counter_1_output, TARGET_ADDRESS;
  wire [17:0] controlled_buffer_3_out, MEM_DATA, multiplexer_1_out;

  Multiplexer #(.select(2), .width(18), .enable("false")) multiplexer_1 (
    .in1(ALU_OUTPUT), .in2(MEM_DATA), .out(multiplexer_1_out), .sel({IS_LD, IS_ALU}));  // open: in0, in3
  Counter #(.width(10), .max('h3ff)) counter_1 (
    .load(ENABLE_JUMP), .D(TARGET_ADDRESS), .count(NEXT_INSTRUCTION), .Q(LAST_ADDRESS),
    .clk(controlled_buffer_1_out));  // open: carry, clr
  assign controlled_buffer_1_out = ENABLE_PC ? CLOCK : 1'bz;  // Controlled_Buffer controlled_buffer_1
  // registerFile registerfile_1: pin names not known; wires that end beside it: multiplexer_1_out, DR_SR_OP2, SR1_OP2, WRITE_ENABLE, CLOCK, SR2, REG1_VALUE, REG2_VALUE, in_1
  Program_Counter program_counter_1 (
    .Enable(ENABLE_JUMP), .Input(TARGET_ADDRESS), .Output(program_counter_1_output),
    .reg_enable(NEXT_INSTRUCTION), .Clock(controlled_buffer_2_out));
  assign controlled_buffer_2_out = ENABLE_PC ? CLOCK : 1'bz;  // Controlled_Buffer controlled_buffer_2
  Program_Counter_3 program_counter_3_1 (
    .\input (TARGET_ADDRESS), .clock(CLOCK), .enable_jump(ENABLE_JUMP), .reset(in_1),
    .next_instruction(ENABLE_PC));  // open: up_down, out_7
  Clock clock_1 (.out(CLOCK));
  ROM #(.addrWidth(10), .dataWidth(20)) rom_1 (.addr(LAST_ADDRESS), .data(out_10));  // open: sel
  not not_1 (not_1_out, CF);
  not not_2 (not_2_out, CF);
  not not_3 (not_3_out, out_8);
  not not_4 (not_4_out, CF);
  not not_5 (not_5_out, CF);
  not not_6 (not_6_out, out_8);
  CPU cpu_1 (
    .Asembly(out_10[19:2]), .IMM_6(IMM_6), .SR2(SR2), .SR1_OP2(SR1_OP2), .ADDRESS(ADDRESS1),
    .DR_SR_OP1(DR_SR_OP2), .ADDRESS2(ADDRESS2), .ALU_CODE(out_11), .IS_ALU(IS_ALU), .IS_IMMEDIATE(IS_IMM),
    .IS_JUMP(IS_JUMP), .IS_LD(IS_LD), .IS_ST(IS_ST), .IS_CMP(IS_CMP), .IS_JE(IS_JE), .IS_JA(IS_JA),
    .IS_JAE(IS_JAE), .IS_JBE(IS_JBE), .IS_JB(IS_JB));  // open: CONSTANT_1
  and and_1 (and_1_out, not_1_out, IS_JBE);
  and and_2 (and_2_out, not_2_out, IS_JAE);
  and and_3 (and_3_out, not_3_out, not_4_out, IS_JA);
  and and_4 (and_4_out, out_8, not_5_out, IS_JE);
  and and_5 (and_5_out, not_6_out, CF, IS_JB);
  assign controlled_buffer_3_out = not_7_out ? REG2_VALUE : 18'bz;  // Controlled_Buffer controlled_buffer_3
  not not_7 (not_7_out, IS_IMM);
  _18_Bit_Comparer u_18_bit_comparer_1 (
    .A(REG1_VALUE), .B(REG2_VALUE), .A_B(n18_bit_comparer_1_a_b[0]), .A_B_2(n18_bit_comparer_1_a_b[1]),
    .A_B_3(n18_bit_comparer_1_a_b[2]));
  Multiplexer #(.select(3), .width(2), .enable("false")) multiplexer_2 (
    .in1(2'b01), .in2(2'b10), .in4(2'b00), .out(multiplexer_2_out), .sel(n18_bit_comparer_1_a_b));  // open: in0, in3, in5, in6, in7
  or or_1 (or_1_out[0], and_1_out, and_2_out, and_3_out, and_4_out, and_5_out);
  \Arıthmetıc_Logic_Unit  \arıthmetıc_logic_unit_1  (
    .Cin(1'b0), .Cout(CF), .A(REG1_VALUE), .B(controlled_buffer_3_out), .IMM(IMM_6), .f(out_11),
    .imm_2(IS_IMM), .out_8(ALU_OUTPUT));
  FSM fsm_1 (
    .clock(CLOCK), .LD(IS_LD), .ST(IS_ST), .JMP(JUMP), .CMP(IS_CMP), .ALU(IS_ALU),
    .enableWrite(WRITE_ENABLE), .enableProgCounter(ENABLE_PC), .nextInstruction(NEXT_INSTRUCTION),
    .enableJump(ENABLE_JUMP));
  assign controlled_buffer_4_out = IS_CMP ? multiplexer_2_out : 2'bz;  // Controlled_Buffer controlled_buffer_4
  D_Latch_Updated d_latch_updated_1 (.D(controlled_buffer_4_out[0]), .c(IS_CMP), .Q(CF));
  D_Latch_Updated d_latch_updated_2 (.D(controlled_buffer_4_out[1]), .c(IS_CMP), .Q(out_8));
  or or_2 (JUMP, IS_JUMP, IS_JUMP, IS_JE, IS_JAE, IS_JBE, IS_JB);
  _10_Bit_Adder ADDER (.Op1(LAST_ADDRESS), .Carry_In(1'b0), .Op2(ADDRESS1), .Sum(ADDER_sum));  // open: Cout
  Multiplexer #(.select(2), .width(10), .enable("false")) multiplexer_3 (
    .in0(LAST_ADDRESS), .in1(ADDRESS1), .in2(ADDER_sum), .out(TARGET_ADDRESS), .sel({IS_JUMP, or_1_out[0]}));  // open: in3
  RAM #(.addrWidth(10), .dataWidth(18), .bus("separate")) ram_1 (
    .addr(ADDRESS2), .din(REG1_VALUE), .data(MEM_DATA), .str(IS_ST), .ld(IS_LD));  // open: sel, clk, clr
  // NOT_Gate not_8 is placed but not wired

  assign out_9 = CF;

  // Other names for the same wires on the sheet: ALU_CODE[1:0] = out_11; RESET = in_1; ZF = out_8

  // Notes on the sheet:
  //   eger address enable_jump 1 olunca hesaplanmiyosa ilk onun hesaplanmasi lazim 
  //   counterin kablosunu kestim osc hatasi veriyodu
  //   contents of rom_1 (hex, n*v repeats v):
  //   71030 82504 60040 1230 91200 a0300 b1ec0 cc580 dfa00 e6cc0 145d0 26780 39a70 4bcd0 5ef10
  //   CMP
  //   JUMPS
  //   LD/ST Operatios
endmodule

module NAND (
  input  in_1,
  input  in_2,
  output out_3
);

  wire and_1_out;

  and and_1 (and_1_out, in_1, in_2);
  not not_1 (out_3, and_1_out);
endmodule

module NOR (
  input  in_1,
  input  in_2,
  output out_3
);

  wire or_1_out;

  or or_1 (or_1_out, in_1, in_2);
  not not_1 (out_3, or_1_out);
endmodule

module D_Latch (
  input  D,
  input  C,
  output Qb
);

  wire and_1_out, and_2_out, nor_1_out;

  and and_1 (and_1_out, D, C);
  and and_2 (and_2_out, C, ~D);  // AND_Gate
  nor nor_1 (nor_1_out, and_1_out, Qb);
  nor nor_2 (Qb, nor_1_out, and_2_out);
endmodule

module D_Flip_Flop (
  input  D,
  input  Clk,
  output Q
);

  wire d_latch_1_qb, not_1_out;

  not not_1 (not_1_out, Clk);
  D_Latch d_latch_1 (.D(D), .C(not_1_out), .Qb(d_latch_1_qb));
  D_Latch d_latch_2 (.D(d_latch_1_qb), .C(Clk), .Qb(Q));
endmodule

module _18_Bit_Register (
  input  [17:0] Input,
  input  Enable,
  input  Clk,
  output [17:0] out_4
);

  wire and_1_out, and_2_out, and_3_out, and_4_out, and_5_out, and_6_out, and_7_out, and_8_out, and_9_out,
       and_10_out, and_11_out, and_12_out, and_13_out, and_14_out, and_15_out, and_16_out, and_17_out,
       and_18_out;

  and and_1 (and_1_out, Input[0], Enable);
  and and_2 (and_2_out, Input[1], Enable);
  and and_3 (and_3_out, Input[2], Enable);
  and and_4 (and_4_out, Input[3], Enable);
  and and_5 (and_5_out, Input[4], Enable);
  and and_6 (and_6_out, Input[5], Enable);
  and and_7 (and_7_out, Input[6], Enable);
  and and_8 (and_8_out, Input[7], Enable);
  and and_9 (and_9_out, Input[8], Enable);
  and and_10 (and_10_out, Input[9], Enable);
  and and_11 (and_11_out, Input[10], Enable);
  and and_12 (and_12_out, Input[11], Enable);
  and and_13 (and_13_out, Input[12], Enable);
  and and_14 (and_14_out, Input[13], Enable);
  and and_15 (and_15_out, Input[14], Enable);
  and and_16 (and_16_out, Input[15], Enable);
  and and_17 (and_17_out, Input[16], Enable);
  and and_18 (and_18_out, Input[17], Enable);
  D_Latch_Updated d_latch_updated_1 (.D(and_1_out), .c(Clk), .Q(out_4[0]));
  D_Latch_Updated d_latch_updated_2 (.D(and_2_out), .c(Clk), .Q(out_4[1]));
  D_Latch_Updated d_latch_updated_3 (.D(and_3_out), .c(Clk), .Q(out_4[2]));
  D_Latch_Updated d_latch_updated_4 (.D(and_4_out), .c(Clk), .Q(out_4[3]));
  D_Latch_Updated d_latch_updated_5 (.D(and_5_out), .c(Clk), .Q(out_4[4]));
  D_Latch_Updated d_latch_updated_6 (.D(and_6_out), .c(Clk), .Q(out_4[5]));
  D_Latch_Updated d_latch_updated_7 (.D(and_7_out), .c(Clk), .Q(out_4[6]));
  D_Latch_Updated d_latch_updated_8 (.D(and_8_out), .c(Clk), .Q(out_4[7]));
  D_Latch_Updated d_latch_updated_9 (.D(and_9_out), .c(Clk), .Q(out_4[8]));
  D_Latch_Updated d_latch_updated_10 (.D(and_10_out), .c(Clk), .Q(out_4[9]));
  D_Latch_Updated d_latch_updated_11 (.D(and_11_out), .c(Clk), .Q(out_4[10]));
  D_Latch_Updated d_latch_updated_12 (.D(and_12_out), .c(Clk), .Q(out_4[11]));
  D_Latch_Updated d_latch_updated_13 (.D(and_13_out), .c(Clk), .Q(out_4[12]));
  D_Latch_Updated d_latch_updated_14 (.D(and_14_out), .c(Clk), .Q(out_4[13]));
  D_Latch_Updated d_latch_updated_15 (.D(and_15_out), .c(Clk), .Q(out_4[14]));
  D_Latch_Updated d_latch_updated_16 (.D(and_16_out), .c(Clk), .Q(out_4[15]));
  D_Latch_Updated d_latch_updated_17 (.D(and_17_out), .c(Clk), .Q(out_4[16]));
  D_Latch_Updated d_latch_updated_18 (.D(and_18_out), .c(Clk), .Q(out_4[17]));
endmodule

module _10_Bit_Register (
  input  [9:0] Input,
  input  Enable,
  input  Clk,
  output [9:0] out_4
);

  wire and_1_out, and_2_out, and_3_out, and_4_out, and_5_out, and_6_out, and_7_out, and_8_out, and_9_out,
       and_10_out;

  and and_1 (and_1_out, Input[0], Enable);
  and and_2 (and_2_out, Input[1], Enable);
  and and_3 (and_3_out, Input[2], Enable);
  and and_4 (and_4_out, Input[3], Enable);
  and and_5 (and_5_out, Input[4], Enable);
  and and_6 (and_6_out, Input[5], Enable);
  and and_7 (and_7_out, Input[6], Enable);
  and and_8 (and_8_out, Input[7], Enable);
  and and_9 (and_9_out, Input[8], Enable);
  and and_10 (and_10_out, Input[9], Enable);
  D_Latch_Updated d_latch_updated_1 (.D(and_1_out), .c(Clk), .Q(out_4[0]));
  D_Latch_Updated d_latch_updated_2 (.D(and_2_out), .c(Clk), .Q(out_4[1]));
  D_Latch_Updated d_latch_updated_3 (.D(and_3_out), .c(Clk), .Q(out_4[2]));
  D_Latch_Updated d_latch_updated_4 (.D(and_4_out), .c(Clk), .Q(out_4[3]));
  D_Latch_Updated d_latch_updated_5 (.D(and_5_out), .c(Clk), .Q(out_4[4]));
  D_Latch_Updated d_latch_updated_6 (.D(and_6_out), .c(Clk), .Q(out_4[5]));
  D_Latch_Updated d_latch_updated_7 (.D(and_7_out), .c(Clk), .Q(out_4[6]));
  D_Latch_Updated d_latch_updated_8 (.D(and_8_out), .c(Clk), .Q(out_4[7]));
  D_Latch_Updated d_latch_updated_9 (.D(and_9_out), .c(Clk), .Q(out_4[8]));
  D_Latch_Updated d_latch_updated_10 (.D(and_10_out), .c(Clk), .Q(out_4[9]));
endmodule

// Register File
module registerFile (
  input  [3:0] read_register1,
  input  [17:0] Input,
  input  reset,
  input  [3:0] write_register,
  input  write_enable,
  input  clock,
  input  [3:0] read_register2,
  output [17:0] Reg1,
  output [17:0] Reg2
);

  wire and_1_out, and_2_out, and_3_out, and_4_out, and_5_out, and_6_out, and_7_out, and_8_out, and_9_out,
       and_10_out, and_11_out, and_12_out, and_13_out, and_14_out, and_15_out, and_16_out, decoder_1_out0,
       decoder_1_out1, decoder_1_out2, decoder_1_out3, decoder_1_out4, decoder_1_out5, decoder_1_out6,
       decoder_1_out7, decoder_1_out8, decoder_1_out9, decoder_1_out10, decoder_1_out11, decoder_1_out12,
       decoder_1_out13, decoder_1_out14, decoder_1_out15, decoder_2_out0, decoder_2_out1, decoder_2_out2,
       decoder_2_out3, decoder_2_out4, decoder_2_out5, decoder_2_out6, decoder_2_out7, decoder_2_out8,
       decoder_2_out9, decoder_2_out10, decoder_2_out11, decoder_2_out12, decoder_2_out13, decoder_2_out14,
       decoder_2_out15, decoder_3_out0, decoder_3_out1, decoder_3_out2, decoder_3_out3, decoder_3_out4,
       decoder_3_out5, decoder_3_out6, decoder_3_out7, decoder_3_out8, decoder_3_out9, decoder_3_out10,
       decoder_3_out11, decoder_3_out12, decoder_3_out13, decoder_3_out14, decoder_3_out15;
  wire [17:0] multiplexer_1_out, n18_bit_register_1_out_4, n18_bit_register_2_out_4,
       n18_bit_register_3_out_4, n18_bit_register_4_out_4, n18_bit_register_5_out_4,
       n18_bit_register_6_out_4, n18_bit_register_7_out_4, n18_bit_register_8_out_4,
       n18_bit_register_9_out_4, n18_bit_register_10_out_4, n18_bit_register_11_out_4,
       n18_bit_register_12_out_4, n18_bit_register_13_out_4, n18_bit_register_14_out_4,
       n18_bit_register_15_out_4, n18_bit_register_16_out_4;

  Decoder #(.select(4), .enable("false")) decoder_1 (
    .out0(decoder_1_out0), .out1(decoder_1_out1), .out2(decoder_1_out2), .out3(decoder_1_out3),
    .out4(decoder_1_out4), .out5(decoder_1_out5), .out6(decoder_1_out6), .out7(decoder_1_out7),
    .out8(decoder_1_out8), .out9(decoder_1_out9), .out10(decoder_1_out10), .out11(decoder_1_out11),
    .out12(decoder_1_out12), .out13(decoder_1_out13), .out14(decoder_1_out14), .out15(decoder_1_out15),
    .sel(read_register1));
  Decoder #(.select(4), .enable("false")) decoder_2 (
    .out0(decoder_2_out0), .out1(decoder_2_out1), .out2(decoder_2_out2), .out3(decoder_2_out3),
    .out4(decoder_2_out4), .out5(decoder_2_out5), .out6(decoder_2_out6), .out7(decoder_2_out7),
    .out8(decoder_2_out8), .out9(decoder_2_out9), .out10(decoder_2_out10), .out11(decoder_2_out11),
    .out12(decoder_2_out12), .out13(decoder_2_out13), .out14(decoder_2_out14), .out15(decoder_2_out15),
    .sel(write_register));
  Decoder #(.select(4), .enable("false")) decoder_3 (
    .out0(decoder_3_out0), .out1(decoder_3_out1), .out2(decoder_3_out2), .out3(decoder_3_out3),
    .out4(decoder_3_out4), .out5(decoder_3_out5), .out6(decoder_3_out6), .out7(decoder_3_out7),
    .out8(decoder_3_out8), .out9(decoder_3_out9), .out10(decoder_3_out10), .out11(decoder_3_out11),
    .out12(decoder_3_out12), .out13(decoder_3_out13), .out14(decoder_3_out14), .out15(decoder_3_out15),
    .sel(read_register2));
  Multiplexer #(.width(18), .enable("false")) multiplexer_1 (
    .in0(Input), .in1({18{1'b0}}), .out(multiplexer_1_out), .sel(reset));
  and and_1 (and_1_out, decoder_2_out0, write_enable);
  and and_2 (and_2_out, decoder_2_out1, write_enable);
  and and_3 (and_3_out, decoder_2_out2, write_enable);
  and and_4 (and_4_out, decoder_2_out3, write_enable);
  and and_5 (and_5_out, decoder_2_out4, write_enable);
  and and_6 (and_6_out, decoder_2_out5, write_enable);
  and and_7 (and_7_out, decoder_2_out6, write_enable);
  and and_8 (and_8_out, decoder_2_out7, write_enable);
  _18_Bit_Register u_18_bit_register_1 (
    .Input(multiplexer_1_out), .Enable(and_1_out), .Clk(clock), .out_4(n18_bit_register_1_out_4));
  _18_Bit_Register u_18_bit_register_2 (
    .Input(multiplexer_1_out), .Enable(and_2_out), .Clk(clock), .out_4(n18_bit_register_2_out_4));
  _18_Bit_Register u_18_bit_register_3 (
    .Input(multiplexer_1_out), .Enable(and_3_out), .Clk(clock), .out_4(n18_bit_register_3_out_4));
  _18_Bit_Register u_18_bit_register_4 (
    .Input(multiplexer_1_out), .Enable(and_4_out), .Clk(clock), .out_4(n18_bit_register_4_out_4));
  _18_Bit_Register u_18_bit_register_5 (
    .Input(multiplexer_1_out), .Enable(and_5_out), .Clk(clock), .out_4(n18_bit_register_5_out_4));
  _18_Bit_Register u_18_bit_register_6 (
    .Input(multiplexer_1_out), .Enable(and_6_out), .Clk(clock), .out_4(n18_bit_register_6_out_4));
  _18_Bit_Register u_18_bit_register_7 (
    .Input(multiplexer_1_out), .Enable(and_7_out), .Clk(clock), .out_4(n18_bit_register_7_out_4));
  _18_Bit_Register u_18_bit_register_8 (
    .Input(multiplexer_1_out), .Enable(and_8_out), .Clk(clock), .out_4(n18_bit_register_8_out_4));
  and and_9 (and_9_out, decoder_2_out8, write_enable);
  and and_10 (and_10_out, decoder_2_out9, write_enable);
  and and_11 (and_11_out, decoder_2_out10, write_enable);
  and and_12 (and_12_out, decoder_2_out11, write_enable);
  and and_13 (and_13_out, decoder_2_out12, write_enable);
  and and_14 (and_14_out, decoder_2_out13, write_enable);
  and and_15 (and_15_out, decoder_2_out14, write_enable);
  and and_16 (and_16_out, decoder_2_out15, write_enable);
  _18_Bit_Register u_18_bit_register_9 (
    .Input(multiplexer_1_out), .Enable(and_9_out), .Clk(clock), .out_4(n18_bit_register_9_out_4));
  _18_Bit_Register u_18_bit_register_10 (
    .Input(multiplexer_1_out), .Enable(and_10_out), .Clk(clock), .out_4(n18_bit_register_10_out_4));
  _18_Bit_Register u_18_bit_register_11 (
    .Input(multiplexer_1_out), .Enable(and_11_out), .Clk(clock), .out_4(n18_bit_register_11_out_4));
  _18_Bit_Register u_18_bit_register_12 (
    .Input(multiplexer_1_out), .Enable(and_12_out), .Clk(clock), .out_4(n18_bit_register_12_out_4));
  _18_Bit_Register u_18_bit_register_13 (
    .Input(multiplexer_1_out), .Enable(and_13_out), .Clk(clock), .out_4(n18_bit_register_13_out_4));
  _18_Bit_Register u_18_bit_register_14 (
    .Input(multiplexer_1_out), .Enable(and_14_out), .Clk(clock), .out_4(n18_bit_register_14_out_4));
  _18_Bit_Register u_18_bit_register_15 (
    .Input(multiplexer_1_out), .Enable(and_15_out), .Clk(clock), .out_4(n18_bit_register_15_out_4));
  _18_Bit_Register u_18_bit_register_16 (
    .Input(multiplexer_1_out), .Enable(and_16_out), .Clk(clock), .out_4(n18_bit_register_16_out_4));
  assign Reg1 = decoder_1_out0 ? n18_bit_register_1_out_4 : 18'bz;  // Controlled_Buffer controlled_buffer_1
  assign Reg2 = decoder_3_out0 ? n18_bit_register_1_out_4 : 18'bz;  // Controlled_Buffer controlled_buffer_2
  assign Reg1 = decoder_1_out8 ? n18_bit_register_9_out_4 : 18'bz;  // Controlled_Buffer controlled_buffer_3
  assign Reg2 = decoder_3_out8 ? n18_bit_register_9_out_4 : 18'bz;  // Controlled_Buffer controlled_buffer_4
  assign Reg1 = decoder_1_out1 ? n18_bit_register_2_out_4 : 18'bz;  // Controlled_Buffer controlled_buffer_5
  assign Reg2 = decoder_3_out1 ? n18_bit_register_2_out_4 : 18'bz;  // Controlled_Buffer controlled_buffer_6
  assign Reg1 = decoder_1_out9 ? n18_bit_register_10_out_4 : 18'bz;  // Controlled_Buffer controlled_buffer_7
  assign Reg2 = decoder_3_out9 ? n18_bit_register_10_out_4 : 18'bz;  // Controlled_Buffer controlled_buffer_8
  assign Reg1 = decoder_1_out2 ? n18_bit_register_3_out_4 : 18'bz;  // Controlled_Buffer controlled_buffer_9
  assign Reg2 = decoder_3_out2 ? n18_bit_register_3_out_4 : 18'bz;  // Controlled_Buffer controlled_buffer_10
  assign Reg1 = decoder_1_out10 ? n18_bit_register_11_out_4 : 18'bz;  // Controlled_Buffer controlled_buffer_11
  assign Reg2 = decoder_3_out10 ? n18_bit_register_11_out_4 : 18'bz;  // Controlled_Buffer controlled_buffer_12
  assign Reg1 = decoder_1_out3 ? n18_bit_register_4_out_4 : 18'bz;  // Controlled_Buffer controlled_buffer_13
  assign Reg2 = decoder_3_out3 ? n18_bit_register_4_out_4 : 18'bz;  // Controlled_Buffer controlled_buffer_14
  assign Reg1 = decoder_1_out11 ? n18_bit_register_12_out_4 : 18'bz;  // Controlled_Buffer controlled_buffer_15
  assign Reg2 = decoder_3_out11 ? n18_bit_register_12_out_4 : 18'bz;  // Controlled_Buffer controlled_buffer_16
  assign Reg1 = decoder_1_out4 ? n18_bit_register_5_out_4 : 18'bz;  // Controlled_Buffer controlled_buffer_17
  assign Reg2 = decoder_3_out4 ? n18_bit_register_5_out_4 : 18'bz;  // Controlled_Buffer controlled_buffer_18
  assign Reg1 = decoder_1_out12 ? n18_bit_register_13_out_4 : 18'bz;  // Controlled_Buffer controlled_buffer_19
  assign Reg2 = decoder_3_out12 ? n18_bit_register_13_out_4 : 18'bz;  // Controlled_Buffer controlled_buffer_20
  assign Reg1 = decoder_1_out5 ? n18_bit_register_6_out_4 : 18'bz;  // Controlled_Buffer controlled_buffer_21
  assign Reg2 = decoder_3_out5 ? n18_bit_register_6_out_4 : 18'bz;  // Controlled_Buffer controlled_buffer_22
  assign Reg1 = decoder_1_out13 ? n18_bit_register_14_out_4 : 18'bz;  // Controlled_Buffer controlled_buffer_23
  assign Reg2 = decoder_3_out13 ? n18_bit_register_14_out_4 : 18'bz;  // Controlled_Buffer controlled_buffer_24
  assign Reg1 = decoder_1_out6 ? n18_bit_register_7_out_4 : 18'bz;  // Controlled_Buffer controlled_buffer_25
  assign Reg2 = decoder_3_out6 ? n18_bit_register_7_out_4 : 18'bz;  // Controlled_Buffer controlled_buffer_26
  assign Reg1 = decoder_1_out14 ? n18_bit_register_15_out_4 : 18'bz;  // Controlled_Buffer controlled_buffer_27
  assign Reg2 = decoder_3_out14 ? n18_bit_register_15_out_4 : 18'bz;  // Controlled_Buffer controlled_buffer_28
  assign Reg1 = decoder_1_out7 ? n18_bit_register_8_out_4 : 18'bz;  // Controlled_Buffer controlled_buffer_29
  assign Reg2 = decoder_3_out7 ? n18_bit_register_8_out_4 : 18'bz;  // Controlled_Buffer controlled_buffer_30
  assign Reg1 = decoder_1_out15 ? n18_bit_register_16_out_4 : 18'bz;  // Controlled_Buffer controlled_buffer_31
  assign Reg2 = decoder_3_out15 ? n18_bit_register_16_out_4 : 18'bz;  // Controlled_Buffer controlled_buffer_32
endmodule

module Full_Adder (
  input  A,
  input  B,
  input  C,
  output Sum,
  output Cout
);

  wire and_1_out, and_2_out, xor_1_out;

  xor xor_1 (xor_1_out, A, B);
  and and_1 (and_1_out, B, A);
  xor xor_2 (Sum, xor_1_out, C);
  and and_2 (and_2_out, xor_1_out, C);
  or or_1 (Cout, and_2_out, and_1_out);
endmodule

module _2_Bit_Adder (
  input  [1:0] Op1,
  input  Carry_In,
  input  [1:0] Op2,
  output [1:0] Sum,
  output Cout
);

  wire full_adder_1_cout;

  Full_Adder full_adder_1 (.A(Op1[0]), .B(Op2[0]), .C(Carry_In), .Sum(Sum[0]), .Cout(full_adder_1_cout));
  Full_Adder full_adder_2 (.A(Op1[1]), .B(Op2[1]), .C(full_adder_1_cout), .Sum(Sum[1]), .Cout(Cout));
endmodule

module CPU (
  input  [17:0] Asembly,
  output [5:0] IMM_6,
  output [1:0] ALU_CODE,
  output [3:0] SR2,
  output [3:0] SR1_OP2,
  output [9:0] ADDRESS,
  output IS_IMMEDIATE,
  output [3:0] DR_SR_OP1,
  output IS_ALU,
  output [9:0] ADDRESS2,
  output IS_JUMP,
  output IS_LD,
  output IS_ST,
  output IS_CMP,
  output IS_JE,
  output IS_JA,
  output IS_JAE,
  output IS_JBE,
  output IS_JB,
  output CONSTANT_1
);

  wire ADD, ADDI, AND, ANDI, NAND, NOR;

  Decoder #(.select(4), .enable("false")) decoder_1 (
    .out0(ADD), .out1(ADDI), .out2(AND), .out3(ANDI), .out4(NAND), .out5(NOR), .out6(IS_JUMP), .out7(IS_LD),
    .out8(IS_ST), .out9(IS_CMP), .out10(IS_JE), .out11(IS_JA), .out12(IS_JB), .out13(IS_JAE), .out14(IS_JBE),
    .sel(Asembly[17:14]));  // open: out15
  or or_1 (ALU_CODE[1], ADD, NOR, ADDI);
  or or_2 (IS_IMMEDIATE, ADDI, ANDI);
  or or_3 (IS_ALU, ADD, ADDI, AND, ANDI, NAND, NOR);
  or or_4 (ALU_CODE[0], ADD, ADDI, NAND);

  assign ADDRESS = Asembly[13:4];
  assign ADDRESS2 = Asembly[9:0];
  assign CONSTANT_1 = 1'b1;
  assign DR_SR_OP1 = Asembly[13:10];
  assign IMM_6 = Asembly[5:0];
  assign SR1_OP2 = Asembly[9:6];
  assign SR2 = Asembly[5:2];

  // Other names for the same wires on the sheet: IMM[5:0] = Asembly[5:0]; CMP = IS_CMP; JA = IS_JA; JAE = IS_JAE;
  //   JB = IS_JB; JBE = IS_JBE; JE = IS_JE; JUMP = IS_JUMP; LD = IS_LD; OPCODE[3:0] = Asembly[17:14]; ST = IS_ST
endmodule

module _4_Bit_Adder (
  input  [3:0] Op1,
  input  Carry_In,
  input  [3:0] Op2,
  output [3:0] Sum,
  output Cout
);

  wire n2_bit_adder_1_cout;

  _2_Bit_Adder u_2_bit_adder_1 (
    .Op1(Op1[1:0]), .Carry_In(Carry_In), .Op2(Op2[1:0]), .Sum(Sum[1:0]), .Cout(n2_bit_adder_1_cout));
  _2_Bit_Adder u_2_bit_adder_2 (
    .Op1(Op1[3:2]), .Carry_In(n2_bit_adder_1_cout), .Op2(Op2[3:2]), .Sum(Sum[3:2]), .Cout(Cout));
endmodule

module _8_Bit_Adder (
  input  [7:0] Op1,
  input  Carry_In,
  input  [7:0] Op2,
  output [7:0] Sum,
  output Cout
);

  wire n4_bit_adder_1_cout;

  _4_Bit_Adder u_4_bit_adder_1 (
    .Op1(Op1[3:0]), .Carry_In(Carry_In), .Op2(Op2[3:0]), .Sum(Sum[3:0]), .Cout(n4_bit_adder_1_cout));
  _4_Bit_Adder u_4_bit_adder_2 (
    .Op1(Op1[7:4]), .Carry_In(n4_bit_adder_1_cout), .Op2(Op2[7:4]), .Sum(Sum[7:4]), .Cout(Cout));
endmodule

module _16_Bit_Adder (
  input  [15:0] Op1,
  input  Carry_In,
  input  [15:0] Op2,
  output [15:0] Sum,
  output Cout
);

  wire n8_bit_adder_1_cout;

  _8_Bit_Adder u_8_bit_adder_1 (
    .Op1(Op1[7:0]), .Carry_In(Carry_In), .Op2(Op2[7:0]), .Sum(Sum[7:0]), .Cout(n8_bit_adder_1_cout));
  _8_Bit_Adder u_8_bit_adder_2 (
    .Op1(Op1[15:8]), .Carry_In(n8_bit_adder_1_cout), .Op2(Op2[15:8]), .Sum(Sum[15:8]), .Cout(Cout));
endmodule

module _18_Bit_Adder (
  input  [17:0] Op1,
  input  Carry_In,
  input  [17:0] Op2,
  output [17:0] Sum,
  output Cout
);

  wire n16_bit_adder_1_cout;

  _16_Bit_Adder u_16_bit_adder_1 (
    .Op1(Op1[15:0]), .Carry_In(Carry_In), .Op2(Op2[15:0]), .Sum(Sum[15:0]), .Cout(n16_bit_adder_1_cout));
  _2_Bit_Adder u_2_bit_adder_1 (
    .Op1(Op1[17:16]), .Carry_In(n16_bit_adder_1_cout), .Op2(Op2[17:16]), .Sum(Sum[17:16]), .Cout(Cout));
endmodule

module _10_Bit_Adder (
  input  [9:0] Op1,
  input  Carry_In,
  input  [9:0] Op2,
  output [9:0] Sum,
  output Cout
);

  wire n8_bit_adder_1_cout;

  _8_Bit_Adder u_8_bit_adder_1 (
    .Op1(Op1[7:0]), .Carry_In(Carry_In), .Op2(Op2[7:0]), .Sum(Sum[7:0]), .Cout(n8_bit_adder_1_cout));
  _2_Bit_Adder u_2_bit_adder_1 (
    .Op1(Op1[9:8]), .Carry_In(n8_bit_adder_1_cout), .Op2(Op2[9:8]), .Sum(Sum[9:8]), .Cout(Cout));
endmodule

module _2_Bit_Comparer (
  input  [1:0] A,
  input  [1:0] B,
  output A_B,
  output A_B_2,
  output A_B_3
);

  wire and_1_out, and_2_out, and_3_out, and_4_out, and_5_out, and_6_out, not_1_out, not_2_out, not_3_out,
       not_4_out, xnor_1_out, xnor_2_out;

  not not_1 (not_1_out, A[1]);
  not not_2 (not_2_out, A[0]);
  not not_3 (not_3_out, B[1]);
  not not_4 (not_4_out, B[0]);
  and and_1 (and_1_out, not_1_out, B[1]);
  and and_2 (and_2_out, not_2_out, B[1], B[0]);
  and and_3 (and_3_out, not_1_out, not_2_out, B[0]);
  xnor xnor_1 (xnor_1_out, A[1], B[1]);
  xnor xnor_2 (xnor_2_out, A[0], B[0]);
  and and_4 (and_4_out, A[1], not_3_out);
  and and_5 (and_5_out, A[0], not_3_out, not_4_out);
  and and_6 (and_6_out, A[1], A[0], not_4_out);
  or or_1 (A_B, and_1_out, and_2_out, and_3_out);
  and and_7 (A_B_2, xnor_1_out, xnor_2_out);
  or or_2 (A_B_3, and_4_out, and_5_out, and_6_out);
endmodule

module _4_Bit_Comparer (
  input  [3:0] A,
  input  [3:0] B,
  output A_B,
  output A_B_2,
  output A_B_3
);

  wire and_1_out, and_2_out, n2_bit_comparer_1_a_b, n2_bit_comparer_1_a_b_2, n2_bit_comparer_1_a_b_3,
       n2_bit_comparer_2_a_b, n2_bit_comparer_2_a_b_2, n2_bit_comparer_2_a_b_3;

  _2_Bit_Comparer u_2_bit_comparer_1 (
    .A(A[1:0]), .B(B[1:0]), .A_B(n2_bit_comparer_1_a_b), .A_B_2(n2_bit_comparer_1_a_b_2),
    .A_B_3(n2_bit_comparer_1_a_b_3));
  _2_Bit_Comparer u_2_bit_comparer_2 (
    .A(A[3:2]), .B(B[3:2]), .A_B(n2_bit_comparer_2_a_b), .A_B_2(n2_bit_comparer_2_a_b_2),
    .A_B_3(n2_bit_comparer_2_a_b_3));
  and and_1 (and_1_out, n2_bit_comparer_1_a_b, n2_bit_comparer_2_a_b_2);
  and and_2 (and_2_out, n2_bit_comparer_2_a_b_2, n2_bit_comparer_1_a_b_3);
  or or_1 (A_B, and_1_out, n2_bit_comparer_2_a_b);
  and and_3 (A_B_2, n2_bit_comparer_1_a_b_2, n2_bit_comparer_2_a_b_2);
  or or_2 (A_B_3, n2_bit_comparer_2_a_b_3, and_2_out);
endmodule

module _8_Bit_Comparer (
  input  [7:0] A,
  input  [7:0] B,
  output A_B,
  output A_B_2,
  output A_B_3
);

  wire and_1_out, and_2_out, n4_bit_comparer_1_a_b, n4_bit_comparer_1_a_b_2, n4_bit_comparer_1_a_b_3,
       n4_bit_comparer_2_a_b, n4_bit_comparer_2_a_b_2, n4_bit_comparer_2_a_b_3;

  _4_Bit_Comparer u_4_bit_comparer_1 (
    .A(A[3:0]), .B(B[3:0]), .A_B(n4_bit_comparer_1_a_b), .A_B_2(n4_bit_comparer_1_a_b_2),
    .A_B_3(n4_bit_comparer_1_a_b_3));
  _4_Bit_Comparer u_4_bit_comparer_2 (
    .A(A[7:4]), .B(B[7:4]), .A_B(n4_bit_comparer_2_a_b), .A_B_2(n4_bit_comparer_2_a_b_2),
    .A_B_3(n4_bit_comparer_2_a_b_3));
  and and_1 (and_1_out, n4_bit_comparer_1_a_b, n4_bit_comparer_2_a_b_2);
  and and_2 (and_2_out, n4_bit_comparer_2_a_b_2, n4_bit_comparer_1_a_b_3);
  or or_1 (A_B, and_1_out, n4_bit_comparer_2_a_b);
  and and_3 (A_B_2, n4_bit_comparer_1_a_b_2, n4_bit_comparer_2_a_b_2);
  or or_2 (A_B_3, n4_bit_comparer_2_a_b_3, and_2_out);
endmodule

module _16_Bit_Comparer (
  input  [15:0] A,
  input  [15:0] B,
  output A_B,
  output A_B_2,
  output A_B_3
);

  wire and_1_out, and_2_out, n8_bit_comparer_1_a_b, n8_bit_comparer_1_a_b_2, n8_bit_comparer_1_a_b_3,
       n8_bit_comparer_2_a_b, n8_bit_comparer_2_a_b_2, n8_bit_comparer_2_a_b_3;

  _8_Bit_Comparer u_8_bit_comparer_1 (
    .A(A[7:0]), .B(B[7:0]), .A_B(n8_bit_comparer_1_a_b), .A_B_2(n8_bit_comparer_1_a_b_2),
    .A_B_3(n8_bit_comparer_1_a_b_3));
  _8_Bit_Comparer u_8_bit_comparer_2 (
    .A(A[15:8]), .B(B[15:8]), .A_B(n8_bit_comparer_2_a_b), .A_B_2(n8_bit_comparer_2_a_b_2),
    .A_B_3(n8_bit_comparer_2_a_b_3));
  and and_1 (and_1_out, n8_bit_comparer_1_a_b, n8_bit_comparer_2_a_b_2);
  and and_2 (and_2_out, n8_bit_comparer_2_a_b_2, n8_bit_comparer_1_a_b_3);
  or or_1 (A_B, and_1_out, n8_bit_comparer_2_a_b);
  and and_3 (A_B_2, n8_bit_comparer_1_a_b_2, n8_bit_comparer_2_a_b_2);
  or or_2 (A_B_3, n8_bit_comparer_2_a_b_3, and_2_out);
endmodule

module _18_Bit_Comparer (
  input  [17:0] A,
  input  [17:0] B,
  output A_B,
  output A_B_2,
  output A_B_3
);

  wire and_1_out, and_2_out, n2_bit_comparer_1_a_b, n2_bit_comparer_1_a_b_2, n2_bit_comparer_1_a_b_3,
       n16_bit_comparer_1_a_b, n16_bit_comparer_1_a_b_2, n16_bit_comparer_1_a_b_3;

  _16_Bit_Comparer u_16_bit_comparer_1 (
    .A(A[15:0]), .B(B[15:0]), .A_B(n16_bit_comparer_1_a_b), .A_B_2(n16_bit_comparer_1_a_b_2),
    .A_B_3(n16_bit_comparer_1_a_b_3));
  _2_Bit_Comparer u_2_bit_comparer_1 (
    .A(A[17:16]), .B(B[17:16]), .A_B(n2_bit_comparer_1_a_b), .A_B_2(n2_bit_comparer_1_a_b_2),
    .A_B_3(n2_bit_comparer_1_a_b_3));
  and and_1 (and_1_out, n16_bit_comparer_1_a_b, n2_bit_comparer_1_a_b_2);
  and and_2 (and_2_out, n2_bit_comparer_1_a_b_2, n16_bit_comparer_1_a_b_3);
  or or_1 (A_B, and_1_out, n2_bit_comparer_1_a_b);
  and and_3 (A_B_2, n16_bit_comparer_1_a_b_2, n2_bit_comparer_1_a_b_2);
  or or_2 (A_B_3, n2_bit_comparer_1_a_b_3, and_2_out);
endmodule

// Counter
module Program_Counter (
  input  Enable,
  input  [9:0] Input,
  input  reg_enable,
  input  Clock,
  output [9:0] Output
);

  wire not_1_out;
  wire [9:0] controlled_buffer_1_out, n10_bit_adder_1_sum, undriven;

  assign controlled_buffer_1_out = Enable ? Input : 10'bz;  // Controlled_Buffer controlled_buffer_1
  not not_1 (not_1_out, Enable);
  assign controlled_buffer_1_out = not_1_out ? undriven : 10'bz;  // Controlled_Buffer controlled_buffer_2
  _10_Bit_Register u_10_bit_register_1 (
    .Input(controlled_buffer_1_out), .Enable(reg_enable), .Clk(Clock), .out_4(Output));
  _10_Bit_Adder u_10_bit_adder_1 (
    .Op1(Output), .Carry_In(1'b1), .Op2({10{1'b0}}), .Sum(n10_bit_adder_1_sum));  // open: Cout

  // Notes on the sheet:
  //   enable: give input as a output
  //   reg_enable: increment the last output when clock is enabled
endmodule

// ALU
module \Arıthmetıc_Logic_Unit  (
  input  Cin,
  input  [17:0] A,
  input  [17:0] B,
  input  [5:0] IMM,
  input  [1:0] f,
  input  imm_2,
  output Cout,
  output [17:0] out_8
);

  wire and_1_out, not_1_out, not_2_out;
  wire [17:0] ADD_y, AND_NAND_NOR_a_2, controlled_buffer_1_out, Extend_out;

  sign_extension Extend (.IMM(IMM), .OUT(Extend_out));
  assign controlled_buffer_1_out = not_1_out ? B : 18'bz;  // Controlled_Buffer controlled_buffer_1
  assign controlled_buffer_1_out = imm_2 ? Extend_out : 18'bz;  // Controlled_Buffer controlled_buffer_2
  not not_1 (not_1_out, imm_2);
  Arithmetic_Unit ADD (.Cin(Cin), .A(A), .A_2(controlled_buffer_1_out), .Y(ADD_y), .Cout(Cout));
  Logic_Unit AND_NAND_NOR (.A(A), .B(controlled_buffer_1_out), .f0(f[1]), .A_2(AND_NAND_NOR_a_2), .f1(f[0]));
  not not_2 (not_2_out, and_1_out);
  and and_1 (and_1_out, f[0], f[1]);
  Multiplexer #(.width(18), .enable("false")) multiplexer_1 (
    .in0(ADD_y), .in1(AND_NAND_NOR_a_2), .out(out_8), .sel(not_2_out));
endmodule

module Arithmetic_Unit (
  input  Cin,
  input  [17:0] A,
  input  [17:0] A_2,
  output [17:0] Y,
  output Cout
);

  _18_Bit_Adder u_18_bit_adder_1 (.Op1(A), .Carry_In(Cin), .Op2(A_2), .Sum(Y), .Cout(Cout));
endmodule

module Logic_Unit (
  input  [17:0] A,
  input  [17:0] B,
  input  f0,
  input  f1,
  output [17:0] A_2
);

  wire [17:0] and_1_out, nand_1_out, nand_2_out, nand_3_out, nand_4_out, nand_5_out;

  assign and_1_out = A & B;  // AND_Gate and_1, 18 bits wide
  assign nand_1_out = ~(A & B);  // NAND_Gate nand_1, 18 bits wide
  assign nand_2_out = ~(A & A);  // NAND_Gate nand_2, 18 bits wide
  assign nand_3_out = ~(B & B);  // NAND_Gate nand_3, 18 bits wide
  assign nand_4_out = ~(nand_2_out & nand_3_out);  // NAND_Gate nand_4, 18 bits wide
  assign nand_5_out = ~(nand_4_out & nand_4_out);  // NAND_Gate nand_5, 18 bits wide
  Multiplexer #(.select(2), .width(18), .enable("false")) multiplexer_1 (
    .in0(and_1_out), .in1(nand_1_out), .in2(nand_5_out), .in3(B), .out(A_2), .sel({f0, f1}));

  // Notes on the sheet:
  //   NOR/10
  //   AND/00
  //   NAND/01
endmodule

module sign_extension (
  input  [5:0] IMM,
  output [17:0] OUT
);


  assign OUT = {{13{IMM[5]}}, IMM[4:0]};
endmodule

module FSM (
  input  clock,
  input  LD,
  input  ST,
  input  JMP,
  input  CMP,
  input  ALU,
  output enableWrite,
  output enableProgCounter,
  output nextInstruction,
  output enableJump
);

  wire controlled_buffer_1_out, decoder_1_out2, not_1_out, or_1_out, or_2_out;
  wire [1:0] counter_1_q;

  assign controlled_buffer_1_out = or_1_out ? clock : 1'bz;  // Controlled_Buffer controlled_buffer_1
  or or_1 (or_1_out, LD, ST, JMP, CMP, ALU);
  Decoder #(.select(2), .enable("false")) decoder_1 (
    .out2(decoder_1_out2), .out3(enableProgCounter), .sel(counter_1_q));  // open: out0, out1
  Counter #(.width(2), .max('h3)) counter_1 (
    .Q(counter_1_q), .clk(controlled_buffer_1_out));  // open: load, D, count, carry, clr
  assign enableJump = JMP ? enableProgCounter : 1'bz;  // Controlled_Buffer controlled_buffer_2
  Multiplexer #(.enable("false")) multiplexer_1 (
    .in0(not_1_out), .in1(enableProgCounter), .out(nextInstruction), .sel(not_1_out));
  not not_1 (not_1_out, JMP);
  assign enableWrite = or_2_out ? decoder_1_out2 : 1'bz;  // Controlled_Buffer controlled_buffer_3
  or or_2 (or_2_out, LD, ALU);
endmodule

module D_Latch_Updated (
  input  D,
  input  c,
  output Q
);

  wire and_1_out, and_2_out, half_adder_1_c_out, half_adder_1_sum, multiplexer_1_out, nand_1_out, nor_1_out,
       not_1_out, register_1_q;

  not not_1 (not_1_out, D);
  Half_Adder half_adder_1 (.A(c), .B(register_1_q), .sum(half_adder_1_sum), .c_out(half_adder_1_c_out));
  and and_1 (and_1_out, D, c);
  and and_2 (and_2_out, c, not_1_out);
  nand nand_1 (nand_1_out, half_adder_1_sum, half_adder_1_c_out);
  Register #(.width(1)) register_1 (.D(nand_1_out), .en(1'b1), .Q(register_1_q), .clk(c));  // open: clr
  nor nor_1 (nor_1_out, and_1_out, Q);
  nor nor_2 (Q, multiplexer_1_out, and_2_out);
  Multiplexer #(.enable("false")) multiplexer_1 (
    .in0(1'b1), .in1(nor_1_out), .out(multiplexer_1_out), .sel(register_1_q));
endmodule

module Half_Adder (
  input  A,
  input  B,
  output sum,
  output c_out
);

  xor xor_1 (sum, A, B);
  and and_1 (c_out, A, B);
endmodule

module FSM_OLD (
  input  clock,
  input  LD,
  input  ST,
  input  JMP,
  input  CMP,
  input  ALU,
  output enableWrite,
  output enableProgCounter,
  output nextInstruction,
  output enableJump
);

  wire alu_nextInst, alu_write, cmp_nextInst, controlled_buffer_1_out, controlled_buffer_2_out,
       controlled_buffer_3_out, controlled_buffer_4_out, controlled_buffer_5_out, counter_3_q,
       decoder_1_out0, decoder_1_out2, decoder_2_out0, decoder_2_out2, decoder_3_out0, decoder_3_out1,
       decoder_4_out0, decoder_4_out3, decoder_5_out1, decoder_5_out2, jump_jumpEnable_1, ld_nextInst,
       ld_write, st_nextInst;
  wire [1:0] counter_1_q, counter_2_q, counter_4_q, counter_5_q;

  Counter #(.width(2), .max('h2)) counter_1 (
    .Q(counter_1_q), .clk(controlled_buffer_1_out));  // open: load, D, count, carry, clr
  assign controlled_buffer_1_out = ALU ? clock : 1'bz;  // Controlled_Buffer controlled_buffer_1
  Counter #(.width(2), .max('h2)) counter_2 (
    .Q(counter_2_q), .clk(controlled_buffer_2_out));  // open: load, D, count, carry, clr
  assign controlled_buffer_2_out = LD ? clock : 1'bz;  // Controlled_Buffer controlled_buffer_2
  Counter #(.width(1), .max('h1)) counter_3 (
    .Q(counter_3_q), .clk(controlled_buffer_3_out));  // open: load, D, count, carry, clr
  assign controlled_buffer_3_out = ST ? clock : 1'bz;  // Controlled_Buffer controlled_buffer_3
  Counter #(.width(2), .max('h3)) counter_4 (
    .Q(counter_4_q), .clk(controlled_buffer_4_out));  // open: load, D, count, carry, clr
  assign controlled_buffer_4_out = CMP ? clock : 1'bz;  // Controlled_Buffer controlled_buffer_4
  Counter #(.width(2), .max('h3)) counter_5 (
    .Q(counter_5_q), .clk(controlled_buffer_5_out));  // open: load, D, count, carry, clr
  assign controlled_buffer_5_out = JMP ? clock : 1'bz;  // Controlled_Buffer controlled_buffer_5
  assign alu_nextInst = decoder_1_out0 ? 1'b0 : 1'bz;  // Controlled_Buffer controlled_buffer_6
  Decoder #(.select(2), .enable("false")) decoder_1 (
    .out0(decoder_1_out0), .out1(alu_write), .out2(decoder_1_out2), .sel(counter_1_q));  // open: out3
  assign alu_nextInst = decoder_1_out2 ? 1'b1 : 1'bz;  // Controlled_Buffer controlled_buffer_7
  assign ld_nextInst = decoder_2_out0 ? 1'b0 : 1'bz;  // Controlled_Buffer controlled_buffer_8
  Decoder #(.select(2), .enable("false")) decoder_2 (
    .out0(decoder_2_out0), .out1(ld_write), .out2(decoder_2_out2), .sel(counter_2_q));  // open: out3
  assign ld_nextInst = decoder_2_out2 ? 1'b1 : 1'bz;  // Controlled_Buffer controlled_buffer_9
  assign st_nextInst = decoder_3_out0 ? 1'b0 : 1'bz;  // Controlled_Buffer controlled_buffer_10
  Decoder #(.enable("false")) decoder_3 (.out0(decoder_3_out0), .out1(decoder_3_out1), .sel(counter_3_q));
  assign st_nextInst = decoder_3_out1 ? 1'b1 : 1'bz;  // Controlled_Buffer controlled_buffer_11
  assign cmp_nextInst = decoder_4_out0 ? 1'b0 : 1'bz;  // Controlled_Buffer controlled_buffer_12
  Decoder #(.select(2), .enable("false")) decoder_4 (
    .out0(decoder_4_out0), .out3(decoder_4_out3), .sel(counter_4_q));  // open: out1, out2
  assign cmp_nextInst = decoder_4_out3 ? 1'b1 : 1'bz;  // Controlled_Buffer controlled_buffer_13
  assign jump_jumpEnable_1 = decoder_5_out1 ? 1'b1 : 1'bz;  // Controlled_Buffer controlled_buffer_14
  Decoder #(.select(2), .enable("false")) decoder_5 (
    .out1(decoder_5_out1), .out2(decoder_5_out2), .sel(counter_5_q));  // open: out0, out3
  assign jump_jumpEnable_1 = decoder_5_out2 ? 1'b0 : 1'bz;  // Controlled_Buffer controlled_buffer_15
  or or_1 (enableWrite, alu_write, ld_write);
  or or_2 (enableProgCounter, alu_nextInst, ld_nextInst, st_nextInst, cmp_nextInst, jump_jumpEnable_1);
  or or_3 (nextInstruction, alu_nextInst, ld_nextInst, cmp_nextInst, st_nextInst);
  or or_4 (enableJump, jump_jumpEnable_1, jump_jumpEnable_1);

  // Other names for the same wires on the sheet: alu_progCounter = alu_nextInst; cmp_progCounter = cmp_nextInst;
  //   jump_jumpEnable_2 = jump_jumpEnable_1; jump_progCounter = jump_jumpEnable_1; ld_progCounter = ld_nextInst;
  //   st_progCounter = st_nextInst

  // Notes on the sheet:
  //   ALU
  //   LD
  //   ST
  //   CMP
  //   JUMP
endmodule

module Program_Counter_2 (
  input  nextAddr,
  input  enableJump,
  input  enablBranch,
  input  clock,
  input  reset,
  input  [17:0] jumpAddr,
  input  [17:0] branchAddr,
  output [17:0] \output 
);

  wire and_1_out, or_1_out;
  wire [17:0] multiplexer_1_out, result;

  or or_1 (or_1_out, enableJump, enablBranch);
  and and_1 (and_1_out, ~nextAddr, or_1_out);  // AND_Gate
  Counter #(.width(18), .max('h3ffff)) counter_1 (
    .load(and_1_out), .D(result), .count(nextAddr), .Q(\output ), .clk(clock), .clr(reset));  // open: carry
  Multiplexer #(.width(18)) multiplexer_1 (
    .in0(jumpAddr), .in1(branchAddr), .out(multiplexer_1_out), .sel(enablBranch), .en(enableJump));
  _18_Bit_Adder u_18_bit_adder_1 (
    .Op1(\output ), .Carry_In(1'b0), .Op2(multiplexer_1_out), .Sum(result));  // open: Cout

  // Other names for the same wires on the sheet: enableBranch = enablBranch
endmodule

module Program_Counter_3 (
  input  [9:0] \input ,
  input  enable_jump,
  input  next_instruction,
  input  reset,
  input  clock,
  input  up_down,
  output [9:0] out_7
);

  wire [9:0] controlled_buffer_1_out, multiplexer_1_out, multiplexer_2_out, multiplexer_3_out,
       n10_bit_adder_1_sum;

  Multiplexer #(.width(10), .enable("false")) multiplexer_1 (
    .in0(n10_bit_adder_1_sum), .in1(\input ), .out(multiplexer_1_out), .sel(enable_jump));
  Multiplexer #(.width(10), .enable("false")) multiplexer_2 (
    .in0(multiplexer_1_out), .in1({10{1'b0}}), .out(multiplexer_2_out), .sel(reset));
  assign controlled_buffer_1_out = next_instruction ? multiplexer_2_out : 10'bz;  // Controlled_Buffer controlled_buffer_1
  D_Flip_Flop d_flip_flop_1 (.D(controlled_buffer_1_out[9]), .Clk(clock), .Q(out_7[9]));
  D_Flip_Flop d_flip_flop_2 (.D(controlled_buffer_1_out[8]), .Clk(clock), .Q(out_7[8]));
  D_Flip_Flop d_flip_flop_3 (.D(controlled_buffer_1_out[7]), .Clk(clock), .Q(out_7[7]));
  D_Flip_Flop d_flip_flop_4 (.D(controlled_buffer_1_out[6]), .Clk(clock), .Q(out_7[6]));
  D_Flip_Flop d_flip_flop_5 (.D(controlled_buffer_1_out[5]), .Clk(clock), .Q(out_7[5]));
  D_Flip_Flop d_flip_flop_6 (.D(controlled_buffer_1_out[4]), .Clk(clock), .Q(out_7[4]));
  D_Flip_Flop d_flip_flop_7 (.D(controlled_buffer_1_out[3]), .Clk(clock), .Q(out_7[3]));
  D_Flip_Flop d_flip_flop_8 (.D(controlled_buffer_1_out[2]), .Clk(clock), .Q(out_7[2]));
  D_Flip_Flop d_flip_flop_9 (.D(controlled_buffer_1_out[1]), .Clk(clock), .Q(out_7[1]));
  Multiplexer #(.width(10), .enable("false")) multiplexer_3 (
    .in0(10'h1), .in1({10{1'b1}}), .out(multiplexer_3_out), .sel(up_down));
  D_Flip_Flop d_flip_flop_10 (.D(controlled_buffer_1_out[0]), .Clk(clock), .Q(out_7[0]));
  _10_Bit_Adder u_10_bit_adder_1 (
    .Op1(out_7), .Carry_In(1'b0), .Op2(multiplexer_3_out), .Sum(n10_bit_adder_1_sum));  // open: Cout
endmodule
